# Fritzing sketch watermeter (saved by Fritzing 0.9.9b)
breadboards: 1

parts:
  Part1 = I2C level shifter bidirectional
  M1 = RioRand LM2596
  M2 = LJ12A3-4-Z [package=THT]
  U1 = NodeMCU V1.0

nets:
  GND: Part1.GND, Part1.HV1, Part1.HV, M1.Pin_1, M1.Pin_2, M1.Pin_4, M2.signal, U1.GND
  N1: Part1.LV, M1.Pin_3, U1.Vin
  N2: Part1.LV1, U1.D1

custom parts:
  LJ12A3-4-Z: LJ12A3-4-Z Proximity Sensor module.220V normally open.
  NodeMCU V1.0: ESP8266 based NodeMCU
